// Logisim project Decodificador.circ as structural Verilog: 1 circuit, main circuit main
module main (
  input  [19:0] in_1,
  input  Control,
  output [7:0] Bus_de_Datos
);

  wire and_1_out, nand_1_out;

  and and_1 (and_1_out, in_1[11], in_1[12], in_1[13], ~in_1[14], in_1[15], in_1[16], in_1[17], in_1[18], in_1[19]);  // AND_Gate
  nand nand_1 (nand_1_out, ~and_1_out, ~Control);  // NAND_Gate
  ROM #(.addrWidth(20)) rom_1 (.addr(in_1), .data(Bus_de_Datos), .sel(nand_1_out));

  // Notes on the sheet:
  //   Bus de Direcciones
  //   Decodificador 
  //   RD
endmodule
