// Logisim project Practica 0.circ as structural Verilog: 1 circuit, main circuit main
module main (
  input  in_1
);

  wire A_q, and_1_out, and_2_out, B_qn, C_q, C_qn, clock_1_out, n74ls47_1_a_2, n74ls47_1_b_2, n74ls47_1_c_2,
       n74ls47_1_d, n74ls47_1_e, n74ls47_1_f, n74ls47_1_g, or_1_out;

  Clock clock_1 (.out(clock_1_out));
  and and_1 (and_1_out, C_qn, B_qn, A_q);
  D_Flip_Flop C (.clk(clock_1_out), .D(and_1_out), .Q(C_q), .Qn(C_qn), .preset(1'b0), .en(1'b1), .reset(in_1));
  D_Flip_Flop B (.clk(clock_1_out), .D(or_1_out), .Qn(B_qn), .preset(1'b0), .en(1'b1), .reset(in_1));  // open: Q
  or or_1 (or_1_out, C_q, A_q);
  and and_2 (and_2_out, B_qn, C_qn);
  D_Flip_Flop A (.clk(clock_1_out), .D(and_2_out), .Q(A_q), .preset(1'b0), .en(1'b1), .reset(in_1));  // open: Qn
  _74ls47 u_74ls47_1 (
    .C(and_1_out), .B(or_1_out), .A(and_2_out), .a_2(n74ls47_1_a_2), .b_2(n74ls47_1_b_2),
    .c_2(n74ls47_1_c_2), .d(n74ls47_1_d), .e(n74ls47_1_e), .f(n74ls47_1_f), .g(n74ls47_1_g));
  _7_Segment_Display u_7_segment_display_1 (
    .g(n74ls47_1_g), .f(n74ls47_1_f), .a(n74ls47_1_a_2), .b(n74ls47_1_b_2), .e(n74ls47_1_e), .d(n74ls47_1_d),
    .c(n74ls47_1_c_2));  // open: dp
endmodule
