// Logisim project Memoria 8x6 bits.circ as structural Verilog: 1 circuit, main circuit main
module main (
  input  DE5,
  input  DE4,
  input  DE3,
  input  DE2,
  input  DE1,
  input  DE0,
  input  Dir_0,
  input  Dir1,
  input  Dir2,
  input  SEL,
  input  LEC,
  input  SAL,
  output D5,
  output D4,
  output D3,
  output D2,
  output D1,
  output D0
);

  wire and_1_out, and_2_out, and_3_out, and_4_out, and_5_out, and_6_out, and_7_out, and_8_out, and_9_out,
       and_10_out, and_11_out, and_12_out, and_13_out, and_14_out, and_15_out, and_16_out, and_17_out,
       and_18_out, and_19_out, and_20_out, and_21_out, and_22_out, and_23_out, and_24_out, and_25_out,
       and_26_out, and_27_out, and_28_out, and_29_out, and_30_out, and_31_out, and_32_out, and_33_out,
       and_34_out, and_35_out, and_36_out, and_37_out, and_38_out, and_39_out, and_40_out, and_41_out,
       and_42_out, and_43_out, and_44_out, and_45_out, and_46_out, and_47_out, and_48_out, and_49_out,
       and_50_out, and_51_out, and_52_out, and_53_out, and_54_out, and_55_out, and_56_out, and_57_out,
       and_58_out, and_59_out, and_60_out, and_61_out, and_62_out, and_63_out, and_64_out, and_65_out,
       and_66_out, d_ff_1_q, d_ff_2_q, d_ff_3_q, d_ff_4_q, d_ff_5_q, d_ff_6_q, d_ff_7_q, d_ff_8_q, d_ff_9_q,
       d_ff_10_q, d_ff_11_q, d_ff_12_q, d_ff_13_q, d_ff_14_q, d_ff_15_q, d_ff_16_q, d_ff_17_q, d_ff_18_q,
       d_ff_19_q, d_ff_20_q, d_ff_21_q, d_ff_22_q, d_ff_23_q, d_ff_24_q, d_ff_25_q, d_ff_26_q, d_ff_27_q,
       d_ff_28_q, d_ff_29_q, d_ff_30_q, d_ff_31_q, d_ff_32_q, d_ff_33_q, d_ff_34_q, d_ff_35_q, d_ff_36_q,
       d_ff_37_q, d_ff_38_q, d_ff_39_q, d_ff_40_q, d_ff_41_q, d_ff_42_q, d_ff_43_q, d_ff_44_q, d_ff_45_q,
       d_ff_46_q, d_ff_47_q, d_ff_48_q, not_1_out, not_2_out, not_3_out, not_4_out, not_5_out, not_6_out,
       not_7_out, not_8_out, not_9_out, not_10_out, not_11_out, not_12_out, not_13_out, or_1_out, or_2_out,
       or_3_out, or_4_out, or_5_out, or_6_out;

  not not_1 (not_1_out, Dir_0);
  not not_2 (not_2_out, Dir1);
  and and_1 (and_1_out, not_1_out, not_2_out, not_3_out);
  not not_3 (not_3_out, Dir2);
  not not_4 (not_4_out, Dir_0);
  and and_2 (and_2_out, not_4_out, not_5_out, Dir2);
  not not_5 (not_5_out, Dir1);
  not not_6 (not_6_out, Dir_0);
  and and_3 (and_3_out, not_6_out, Dir1, not_7_out);
  not not_7 (not_7_out, Dir2);
  not not_8 (not_8_out, Dir_0);
  and and_4 (and_4_out, not_8_out, Dir1, Dir2);
  not not_9 (not_9_out, Dir1);
  and and_5 (and_5_out, Dir_0, not_9_out, not_10_out);
  not not_10 (not_10_out, Dir2);
  and and_6 (and_6_out, Dir_0, not_11_out, Dir2);
  not not_11 (not_11_out, Dir1);
  and and_7 (and_7_out, Dir_0, Dir1, not_12_out);
  not not_12 (not_12_out, Dir2);
  and and_8 (and_8_out, Dir2, Dir1, Dir_0);
  and and_9 (and_9_out, SEL, not_13_out);
  not not_13 (not_13_out, LEC);
  and and_10 (and_10_out, and_9_out, and_1_out);
  and and_11 (and_11_out, and_9_out, and_2_out);
  and and_12 (and_12_out, and_9_out, and_3_out);
  and and_13 (and_13_out, and_9_out, and_4_out);
  and and_14 (and_14_out, and_9_out, and_5_out);
  and and_15 (and_15_out, and_9_out, and_6_out);
  and and_16 (and_16_out, and_9_out, and_7_out);
  and and_17 (and_17_out, and_9_out, and_8_out);
  and and_18 (and_18_out, LEC, SEL, SAL);
  D_Flip_Flop d_ff_1 (.clk(and_10_out), .D(DE0), .Q(d_ff_1_q));  // open: Qn, preset, en, reset
  D_Flip_Flop d_ff_2 (.clk(and_11_out), .D(DE0), .Q(d_ff_2_q));  // open: Qn, preset, en, reset
  D_Flip_Flop d_ff_3 (.clk(and_12_out), .D(DE0), .Q(d_ff_3_q));  // open: Qn, preset, en, reset
  D_Flip_Flop d_ff_4 (.clk(and_13_out), .D(DE0), .Q(d_ff_4_q));  // open: Qn, preset, en, reset
  D_Flip_Flop d_ff_5 (.clk(and_14_out), .D(DE0), .Q(d_ff_5_q));  // open: Qn, preset, en, reset
  D_Flip_Flop d_ff_6 (.clk(and_15_out), .D(DE0), .Q(d_ff_6_q));  // open: Qn, preset, en, reset
  D_Flip_Flop d_ff_7 (.clk(and_16_out), .D(DE0), .Q(d_ff_7_q));  // open: Qn, preset, en, reset
  D_Flip_Flop d_ff_8 (.clk(and_17_out), .D(DE0), .Q(d_ff_8_q));  // open: Qn, preset, en, reset
  and and_19 (and_19_out, and_8_out, d_ff_8_q);
  and and_20 (and_20_out, and_4_out, d_ff_4_q);
  and and_21 (and_21_out, and_5_out, d_ff_5_q);
  and and_22 (and_22_out, and_6_out, d_ff_6_q);
  and and_23 (and_23_out, and_7_out, d_ff_7_q);
  or or_1 (or_1_out, and_19_out, and_23_out, and_22_out, and_21_out, and_20_out, and_26_out, and_25_out, and_24_out);
  and and_24 (and_24_out, and_1_out, d_ff_1_q);
  and and_25 (and_25_out, and_2_out, d_ff_2_q);
  and and_26 (and_26_out, and_3_out, d_ff_3_q);
  D_Flip_Flop d_ff_9 (.clk(and_10_out), .D(DE1), .Q(d_ff_9_q));  // open: Qn, preset, en, reset
  D_Flip_Flop d_ff_10 (.clk(and_11_out), .D(DE1), .Q(d_ff_10_q));  // open: Qn, preset, en, reset
  D_Flip_Flop d_ff_11 (.clk(and_12_out), .D(DE1), .Q(d_ff_11_q));  // open: Qn, preset, en, reset
  D_Flip_Flop d_ff_12 (.clk(and_13_out), .D(DE1), .Q(d_ff_12_q));  // open: Qn, preset, en, reset
  D_Flip_Flop d_ff_13 (.clk(and_14_out), .D(DE1), .Q(d_ff_13_q));  // open: Qn, preset, en, reset
  D_Flip_Flop d_ff_14 (.clk(and_15_out), .D(DE1), .Q(d_ff_14_q));  // open: Qn, preset, en, reset
  D_Flip_Flop d_ff_15 (.clk(and_16_out), .D(DE1), .Q(d_ff_15_q));  // open: Qn, preset, en, reset
  D_Flip_Flop d_ff_16 (.clk(and_17_out), .D(DE1), .Q(d_ff_16_q));  // open: Qn, preset, en, reset
  and and_27 (and_27_out, and_5_out, d_ff_13_q);
  and and_28 (and_28_out, and_6_out, d_ff_14_q);
  and and_29 (and_29_out, and_7_out, d_ff_15_q);
  and and_30 (and_30_out, and_8_out, d_ff_16_q);
  or or_2 (or_2_out, and_30_out, and_29_out, and_28_out, and_27_out, and_34_out, and_33_out, and_32_out, and_31_out);
  and and_31 (and_31_out, and_1_out, d_ff_9_q);
  and and_32 (and_32_out, and_2_out, d_ff_10_q);
  and and_33 (and_33_out, and_3_out, d_ff_11_q);
  and and_34 (and_34_out, and_4_out, d_ff_12_q);
  D_Flip_Flop d_ff_17 (.clk(and_10_out), .D(DE2), .Q(d_ff_17_q));  // open: Qn, preset, en, reset
  D_Flip_Flop d_ff_18 (.clk(and_11_out), .D(DE2), .Q(d_ff_18_q));  // open: Qn, preset, en, reset
  D_Flip_Flop d_ff_19 (.clk(and_12_out), .D(DE2), .Q(d_ff_19_q));  // open: Qn, preset, en, reset
  D_Flip_Flop d_ff_20 (.clk(and_13_out), .D(DE2), .Q(d_ff_20_q));  // open: Qn, preset, en, reset
  D_Flip_Flop d_ff_21 (.clk(and_14_out), .D(DE2), .Q(d_ff_21_q));  // open: Qn, preset, en, reset
  D_Flip_Flop d_ff_22 (.clk(and_15_out), .D(DE2), .Q(d_ff_22_q));  // open: Qn, preset, en, reset
  D_Flip_Flop d_ff_23 (.clk(and_16_out), .D(DE2), .Q(d_ff_23_q));  // open: Qn, preset, en, reset
  and and_35 (and_35_out, and_6_out, d_ff_22_q);
  D_Flip_Flop d_ff_24 (.clk(and_17_out), .D(DE2), .Q(d_ff_24_q));  // open: Qn, preset, en, reset
  and and_36 (and_36_out, and_7_out, d_ff_23_q);
  and and_37 (and_37_out, and_8_out, d_ff_24_q);
  or or_3 (or_3_out, and_37_out, and_36_out, and_35_out, and_41_out, and_40_out, and_39_out, and_38_out, and_42_out);
  and and_38 (and_38_out, and_2_out, d_ff_18_q);
  and and_39 (and_39_out, and_3_out, d_ff_19_q);
  and and_40 (and_40_out, and_4_out, d_ff_20_q);
  and and_41 (and_41_out, and_5_out, d_ff_21_q);
  and and_42 (and_42_out, and_1_out, d_ff_17_q);
  D_Flip_Flop d_ff_25 (.clk(and_10_out), .D(DE3), .Q(d_ff_25_q));  // open: Qn, preset, en, reset
  D_Flip_Flop d_ff_26 (.clk(and_11_out), .D(DE3), .Q(d_ff_26_q));  // open: Qn, preset, en, reset
  D_Flip_Flop d_ff_27 (.clk(and_12_out), .D(DE3), .Q(d_ff_27_q));  // open: Qn, preset, en, reset
  D_Flip_Flop d_ff_28 (.clk(and_13_out), .D(DE3), .Q(d_ff_28_q));  // open: Qn, preset, en, reset
  D_Flip_Flop d_ff_29 (.clk(and_14_out), .D(DE3), .Q(d_ff_29_q));  // open: Qn, preset, en, reset
  D_Flip_Flop d_ff_30 (.clk(and_15_out), .D(DE3), .Q(d_ff_30_q));  // open: Qn, preset, en, reset
  and and_43 (and_43_out, and_5_out, d_ff_29_q);
  D_Flip_Flop d_ff_31 (.clk(and_16_out), .D(DE3), .Q(d_ff_31_q));  // open: Qn, preset, en, reset
  and and_44 (and_44_out, and_6_out, d_ff_30_q);
  D_Flip_Flop d_ff_32 (.clk(and_17_out), .D(DE3), .Q(d_ff_32_q));  // open: Qn, preset, en, reset
  and and_45 (and_45_out, and_7_out, d_ff_31_q);
  and and_46 (and_46_out, and_8_out, d_ff_32_q);
  or or_4 (or_4_out, and_46_out, and_45_out, and_44_out, and_43_out, and_50_out, and_49_out, and_48_out, and_47_out);
  and and_47 (and_47_out, and_1_out, d_ff_25_q);
  and and_48 (and_48_out, and_2_out, d_ff_26_q);
  and and_49 (and_49_out, and_3_out, d_ff_27_q);
  and and_50 (and_50_out, and_4_out, d_ff_28_q);
  D_Flip_Flop d_ff_33 (.clk(and_10_out), .D(DE4), .Q(d_ff_33_q));  // open: Qn, preset, en, reset
  D_Flip_Flop d_ff_34 (.clk(and_11_out), .D(DE4), .Q(d_ff_34_q));  // open: Qn, preset, en, reset
  D_Flip_Flop d_ff_35 (.clk(and_12_out), .D(DE4), .Q(d_ff_35_q));  // open: Qn, preset, en, reset
  D_Flip_Flop d_ff_36 (.clk(and_13_out), .D(DE4), .Q(d_ff_36_q));  // open: Qn, preset, en, reset
  D_Flip_Flop d_ff_37 (.clk(and_14_out), .D(DE4), .Q(d_ff_37_q));  // open: Qn, preset, en, reset
  D_Flip_Flop d_ff_38 (.clk(and_15_out), .D(DE4), .Q(d_ff_38_q));  // open: Qn, preset, en, reset
  D_Flip_Flop d_ff_39 (.clk(and_16_out), .D(DE4), .Q(d_ff_39_q));  // open: Qn, preset, en, reset
  D_Flip_Flop d_ff_40 (.clk(and_17_out), .D(DE4), .Q(d_ff_40_q));  // open: Qn, preset, en, reset
  and and_51 (and_51_out, and_5_out, d_ff_37_q);
  and and_52 (and_52_out, and_6_out, d_ff_38_q);
  and and_53 (and_53_out, and_7_out, d_ff_39_q);
  and and_54 (and_54_out, and_8_out, d_ff_40_q);
  or or_5 (or_5_out, and_54_out, and_53_out, and_52_out, and_51_out, and_58_out, and_57_out, and_56_out, and_55_out);
  and and_55 (and_55_out, and_1_out, d_ff_33_q);
  and and_56 (and_56_out, and_2_out, d_ff_34_q);
  and and_57 (and_57_out, and_3_out, d_ff_35_q);
  and and_58 (and_58_out, and_4_out, d_ff_36_q);
  D_Flip_Flop d_ff_41 (.clk(and_10_out), .D(DE5), .Q(d_ff_41_q));  // open: Qn, preset, en, reset
  D_Flip_Flop d_ff_42 (.clk(and_11_out), .D(DE5), .Q(d_ff_42_q));  // open: Qn, preset, en, reset
  D_Flip_Flop d_ff_43 (.clk(and_12_out), .D(DE5), .Q(d_ff_43_q));  // open: Qn, preset, en, reset
  D_Flip_Flop d_ff_44 (.clk(and_13_out), .D(DE5), .Q(d_ff_44_q));  // open: Qn, preset, en, reset
  D_Flip_Flop d_ff_45 (.clk(and_14_out), .D(DE5), .Q(d_ff_45_q));  // open: Qn, preset, en, reset
  D_Flip_Flop d_ff_46 (.clk(and_15_out), .D(DE5), .Q(d_ff_46_q));  // open: Qn, preset, en, reset
  D_Flip_Flop d_ff_47 (.clk(and_16_out), .D(DE5), .Q(d_ff_47_q));  // open: Qn, preset, en, reset
  D_Flip_Flop d_ff_48 (.clk(and_17_out), .D(DE5), .Q(d_ff_48_q));  // open: Qn, preset, en, reset
  assign D0 = and_18_out ? or_1_out : 1'bz;  // Controlled_Buffer controlled_buffer_1
  and and_59 (and_59_out, and_5_out, d_ff_45_q);
  and and_60 (and_60_out, and_6_out, d_ff_46_q);
  and and_61 (and_61_out, and_7_out, d_ff_47_q);
  and and_62 (and_62_out, and_8_out, d_ff_48_q);
  or or_6 (or_6_out, and_62_out, and_61_out, and_60_out, and_59_out, and_66_out, and_65_out, and_64_out, and_63_out);
  assign D2 = and_18_out ? or_3_out : 1'bz;  // Controlled_Buffer controlled_buffer_2
  assign D1 = and_18_out ? or_2_out : 1'bz;  // Controlled_Buffer controlled_buffer_3
  and and_63 (and_63_out, and_1_out, d_ff_41_q);
  and and_64 (and_64_out, and_2_out, d_ff_42_q);
  and and_65 (and_65_out, and_3_out, d_ff_43_q);
  and and_66 (and_66_out, and_4_out, d_ff_44_q);
  assign D4 = and_18_out ? or_5_out : 1'bz;  // Controlled_Buffer controlled_buffer_4
  assign D3 = and_18_out ? or_4_out : 1'bz;  // Controlled_Buffer controlled_buffer_5
  assign D5 = and_18_out ? or_6_out : 1'bz;  // Controlled_Buffer controlled_buffer_6

  // Notes on the sheet:
  //   Decodificador
  //   Habilitación de Salida
  //   Memoria 8 x 6 Basada en Flip-Flops
endmodule
