// Logisim project RAM-1.circ as structural Verilog: 1 circuit, main circuit main
module main (
  input  [10:0] in_1,
  input  [23:0] in_2,
  input  in_3,
  input  in_4,
  input  R_W_prime,
  output [23:0] out_6
);

  wire not_1_out;
  wire [23:0] controlled_buffer_1_out;

  assign controlled_buffer_1_out = not_1_out ? in_2 : 24'bz;  // Controlled_Buffer controlled_buffer_1
  not not_1 (not_1_out, R_W_prime);
  RAM #(.addrWidth(11), .dataWidth(24), .bus("asynch")) ram_1 (
    .addr(in_1), .data(controlled_buffer_1_out), .sel(in_4), .ld(R_W_prime), .clr(in_3));
  assign out_6 = R_W_prime ? controlled_buffer_1_out : 24'bz;  // Controlled_Buffer controlled_buffer_2

  // Notes on the sheet:
  //   Dirección
  //   Entrada
  //   Bus de Direcciones
  //   Bus de Control
  //   Bus de Datos
  //   Salida
endmodule
