// Logisim project RAM-2.circ as structural Verilog: 1 circuit, main circuit main
module main (
  input  [10:0] in_1,
  input  [23:0] in_2,
  input  in_3,
  input  R_W_prime,
  input  Clear,
  output [23:0] out_6
);

  wire not_1_out;
  wire [7:0] ram_1_data, ram_2_data, ram_3_data;

  RAM #(.addrWidth(11), .bus("asynch")) ram_1 (.addr(in_1), .data(ram_1_data), .sel(in_3), .ld(R_W_prime), .clr(Clear));
  RAM #(.addrWidth(11), .bus("asynch")) ram_2 (.addr(in_1), .data(ram_2_data), .sel(in_3), .ld(R_W_prime), .clr(Clear));
  RAM #(.addrWidth(11), .bus("asynch")) ram_3 (.addr(in_1), .data(ram_3_data), .sel(in_3), .ld(R_W_prime), .clr(Clear));
  assign ram_1_data = not_1_out ? in_2[23:16] : 8'bz;  // Controlled_Buffer controlled_buffer_1
  not not_1 (not_1_out, R_W_prime);
  assign out_6 = R_W_prime ? {ram_3_data, ram_2_data, ram_1_data} : 24'bz;  // Controlled_Buffer controlled_buffer_2
  assign ram_2_data = not_1_out ? in_2[15:8] : 8'bz;  // Controlled_Buffer controlled_buffer_3
  assign ram_3_data = not_1_out ? in_2[7:0] : 8'bz;  // Controlled_Buffer controlled_buffer_4

  // Notes on the sheet:
  //   Dirección
  //   Activar / Desactivar
  //   Bus de Direcciones
  //   Bus de Control
  //   Bus de Datos
  //   Salida
  //   Entrada
endmodule
