// Logisim project RAM-parte-3.circ as structural Verilog: 1 circuit, main circuit main
module main (
  input  [10:0] in_1,
  input  Reset,
  input  [23:0] in_3,
  input  R_W_prime,
  output [23:0] out_5
);

  wire not_1_out, not_2_out;
  wire [23:0] controlled_buffer_1_out;

  assign controlled_buffer_1_out = not_2_out ? in_3 : 24'bz;  // Controlled_Buffer controlled_buffer_1
  not not_1 (not_1_out, in_1[10]);
  RAM #(.addrWidth(10), .bus("asynch")) ram_1 (
    .addr(in_1[9:0]), .data(controlled_buffer_1_out[23:16]), .sel(not_1_out), .ld(R_W_prime), .clr(Reset));
  RAM #(.addrWidth(10), .bus("asynch")) ram_2 (
    .addr(in_1[9:0]), .data(controlled_buffer_1_out[23:16]), .sel(in_1[10]), .ld(R_W_prime), .clr(Reset));
  RAM #(.addrWidth(10), .bus("asynch")) ram_3 (
    .addr(in_1[9:0]), .data(controlled_buffer_1_out[15:8]), .sel(not_1_out), .ld(R_W_prime), .clr(Reset));
  RAM #(.addrWidth(10), .bus("asynch")) ram_4 (
    .addr(in_1[9:0]), .data(controlled_buffer_1_out[15:8]), .sel(in_1[10]), .ld(R_W_prime), .clr(Reset));
  not not_2 (not_2_out, R_W_prime);
  RAM #(.addrWidth(10), .bus("asynch")) ram_5 (
    .addr(in_1[9:0]), .data(controlled_buffer_1_out[7:0]), .sel(not_1_out), .ld(R_W_prime), .clr(Reset));
  RAM #(.addrWidth(10), .bus("asynch")) ram_6 (
    .addr(in_1[9:0]), .data(controlled_buffer_1_out[7:0]), .sel(in_1[10]), .ld(R_W_prime), .clr(Reset));
  assign out_5 = R_W_prime ? controlled_buffer_1_out : 24'bz;  // Controlled_Buffer controlled_buffer_2

  // Notes on the sheet:
  //   Dirección
  //   Bit para seleccionar renglón
  //   Entrada
  //   Bus de Direcciones
  //   Más significativo
  //   Más significativo
  //   Bus de Control
  //   Menos significativo
  //   Menos significativo
  //   Bus de Datos
  //   Bus de Datos
  //   Salida
endmodule
