// Logisim project RAMasy2048x24bits.circ as structural Verilog: 1 circuit, main circuit main
module main (
  input  [10:0] in_1,
  input  Selector,
  input  CLR,
  input  [23:0] in_4,
  input  R_W_prime,
  output [23:0] out_6
);

  wire not_1_out;
  wire [23:0] controlled_buffer_1_out;

  assign controlled_buffer_1_out = not_1_out ? in_4 : 24'bz;  // Controlled_Buffer controlled_buffer_1
  not not_1 (not_1_out, R_W_prime);
  RAM #(.addrWidth(11), .dataWidth(24), .bus("asynch")) ram_1 (
    .addr(in_1), .data(controlled_buffer_1_out), .sel(Selector), .ld(R_W_prime), .clr(CLR));
  assign out_6 = R_W_prime ? controlled_buffer_1_out : 24'bz;  // Controlled_Buffer controlled_buffer_2

  // Notes on the sheet:
  //   Dirección
  //   Entrada
  //   Bus de Direcciones de 2048 bits
  //   Memoria RAM asíncrona de 2048 x 24 bits
  //   Bus de Control
  //   Bus de Datos de 24 bits
  //   Salida
endmodule
